# Fritzing sketch Circuit_MAD_Single (saved by Fritzing 0.9.3b)
circuit board: 5cm x 5.5cm

parts:
  mini_5V = Arduino Pro Mini (5V)
  J2 = female pin header, 2 pins [form="♀ (female)"]  # not connected
  J3 = female pin header, 4 pins [form="♀ (female)"]  # not connected
  (+) = Round Pushbutton
  Init = Round Pushbutton
  (-) = Round Pushbutton
  R1 = Resistor [tolerance=±5% resistance=4.7k package=THT]
  R2 = Resistor [tolerance=±5% resistance=10k package=THT]
  Pwr = female pin header, 2 pins [form="♀ (female)"]
  Oled = female pin header, 4 pins [form="♀ (female)"]
  MPU_6050 = female pin header, 4 pins [form="♀ (female)"]

nets:
  N1: mini_5V.VCC, Oled.pin2, MPU_6050.pin2
  N2: mini_5V.A4, Oled.pin3, MPU_6050.pin3
  N3: mini_5V.A5, Oled.pin4, MPU_6050.pin4
  N4: mini_5V.RAW, R1.Pin_1, Pwr.pin2
  N5: mini_5V.GND, (+).leg1, Init.leg1, (-).leg1, R2.Pin_0, Pwr.pin1, Oled.pin1, MPU_6050.pin1
  N6: mini_5V.A3, R1.Pin_0, R2.Pin_1
  N7: mini_5V.D7, (+).leg0
  N8: mini_5V.D6, Init.leg0
  N9: mini_5V.D5, (-).leg0

notes:
  Power between 5V & 12V
  R1 10kΩ
  R2 4,7kΩ
  Push-button (-)
  Push-button Init
  Push-button (+)
  MPU 6050
  Oled ssd1306
  Arduino pro mini 5V
  GND
  RAW
  SDA
  SCL
  5V
  MAD_Single V1.0
  ANEG 2018
